# Fritzing sketch schema (saved by Fritzing 0.9.2b)
circuit board: 8.46667cm x 5.64444cm
breadboards: 1

parts:
  Sensor = Arduino Uno (Rev3)
  R1 = Resistor [tolerance=±5% resistance=22k package=THT]
  R2 = Temperature Sensor (Thermistor) [thermistor_type=NTC package=THT]

nets:
  N1: Sensor.A0, R1.Pin_1, R2.pin_0
  N2: Sensor.GND, R1.Pin_0
  N3: Sensor.5V, R2.pin_1
